// Logisim project Assignment.circ as structural Verilog: 1 circuit, main circuit main
module main (
);

  wire and_1_out, and_2_out, and_3_out, clock_1_out, decoder_1_out0, decoder_1_out1, decoder_1_out2,
       decoder_1_out3, decoder_1_out4, decoder_1_out5, decoder_1_out6, decoder_1_out7, decoder_1_out8,
       decoder_1_out9, decoder_1_out10, decoder_1_out11, decoder_1_out12, decoder_1_out13, decoder_1_out14,
       decoder_1_out15, decoder_1_out16, decoder_1_out17, decoder_1_out18, decoder_1_out19, decoder_1_out20,
       decoder_1_out21, decoder_1_out22, decoder_1_out23, decoder_1_out24, decoder_1_out25, decoder_1_out26,
       decoder_1_out27, decoder_1_out28, decoder_1_out29, decoder_1_out30, decoder_1_out31, or_1_out,
       or_2_out, or_3_out, or_4_out, or_5_out, or_6_out, or_7_out, or_8_out, or_9_out, or_10_out, or_11_out,
       or_12_out;
  wire [4:0] t_ff_5_q;

  Clock clock_1 (.out(clock_1_out));
  and and_1 (and_1_out, t_ff_5_q[3], t_ff_5_q[2], t_ff_5_q[1], t_ff_5_q[0]);
  T_Flip_Flop t_ff_1 (.clk(clock_1_out), .T(and_1_out), .Q(t_ff_5_q[4]));  // open: Qn, preset, reset, en
  and and_2 (and_2_out, t_ff_5_q[2], t_ff_5_q[1], t_ff_5_q[0]);
  or or_1 (or_1_out, decoder_1_out31, decoder_1_out30);
  T_Flip_Flop t_ff_2 (.clk(clock_1_out), .T(and_2_out), .Q(t_ff_5_q[3]));  // open: Qn, preset, reset, en
  T_Flip_Flop t_ff_3 (.clk(clock_1_out), .T(and_3_out), .Q(t_ff_5_q[2]));  // open: Qn, preset, reset, en
  and and_3 (and_3_out, t_ff_5_q[1], t_ff_5_q[0]);
  or or_2 (or_2_out, decoder_1_out29, decoder_1_out28, decoder_1_out27, decoder_1_out26, decoder_1_out25, decoder_1_out24);
  T_Flip_Flop t_ff_4 (.clk(clock_1_out), .T(t_ff_5_q[0]), .Q(t_ff_5_q[1]));  // open: Qn, preset, reset, en
  LED led_1 (.in(or_3_out));
  LED led_2 (.in(or_1_out));
  LED led_3 (.in(or_2_out));
  T_Flip_Flop t_ff_5 (.clk(clock_1_out), .T(1'b1), .Q(t_ff_5_q[0]));  // open: Qn, preset, reset, en
  Decoder #(.select(5), .enable("false")) decoder_1 (
    .out0(decoder_1_out0), .out1(decoder_1_out1), .out2(decoder_1_out2), .out3(decoder_1_out3),
    .out4(decoder_1_out4), .out5(decoder_1_out5), .out6(decoder_1_out6), .out7(decoder_1_out7),
    .out8(decoder_1_out8), .out9(decoder_1_out9), .out10(decoder_1_out10), .out11(decoder_1_out11),
    .out12(decoder_1_out12), .out13(decoder_1_out13), .out14(decoder_1_out14), .out15(decoder_1_out15),
    .out16(decoder_1_out16), .out17(decoder_1_out17), .out18(decoder_1_out18), .out19(decoder_1_out19),
    .out20(decoder_1_out20), .out21(decoder_1_out21), .out22(decoder_1_out22), .out23(decoder_1_out23),
    .out24(decoder_1_out24), .out25(decoder_1_out25), .out26(decoder_1_out26), .out27(decoder_1_out27),
    .out28(decoder_1_out28), .out29(decoder_1_out29), .out30(decoder_1_out30), .out31(decoder_1_out31),
    .sel(t_ff_5_q));
  or or_3 (or_3_out, decoder_1_out23, decoder_1_out22, decoder_1_out21, decoder_1_out20, decoder_1_out19, decoder_1_out18, decoder_1_out17, decoder_1_out16, decoder_1_out15, decoder_1_out14, decoder_1_out13, decoder_1_out12, decoder_1_out11, decoder_1_out10, decoder_1_out9, decoder_1_out8, decoder_1_out7, decoder_1_out6, decoder_1_out5, decoder_1_out4, decoder_1_out3, decoder_1_out2, decoder_1_out1, decoder_1_out0);
  or or_4 (or_4_out, decoder_1_out0, decoder_1_out1, decoder_1_out2, decoder_1_out3, decoder_1_out4, decoder_1_out5);
  LED led_4 (.in(or_4_out));
  LED led_5 (.in(or_9_out));
  or or_5 (or_5_out, decoder_1_out6, decoder_1_out7);
  LED led_6 (.in(or_6_out));
  LED led_7 (.in(or_5_out));
  LED led_8 (.in(or_7_out));
  LED led_9 (.in(or_8_out));
  or or_6 (or_6_out, decoder_1_out8, decoder_1_out9, decoder_1_out10, decoder_1_out11, decoder_1_out12, decoder_1_out13, decoder_1_out14, decoder_1_out15, decoder_1_out16, decoder_1_out17, decoder_1_out18, decoder_1_out19, decoder_1_out20, decoder_1_out21, decoder_1_out22, decoder_1_out23, decoder_1_out24, decoder_1_out25, decoder_1_out26, decoder_1_out27, decoder_1_out28, decoder_1_out29, decoder_1_out30, decoder_1_out31);
  LED led_10 (.in(or_12_out));
  LED led_11 (.in(or_11_out));
  LED led_12 (.in(or_10_out));
  or or_7 (or_7_out, decoder_1_out23, decoder_1_out22);
  or or_8 (or_8_out, decoder_1_out21, decoder_1_out20, decoder_1_out19, decoder_1_out18, decoder_1_out17, decoder_1_out16);
  or or_9 (or_9_out, decoder_1_out31, decoder_1_out30, decoder_1_out29, decoder_1_out28, decoder_1_out27, decoder_1_out26, decoder_1_out25, decoder_1_out24, decoder_1_out15, decoder_1_out14, decoder_1_out13, decoder_1_out12, decoder_1_out11, decoder_1_out10, decoder_1_out9, decoder_1_out8, decoder_1_out7, decoder_1_out6, decoder_1_out5, decoder_1_out4, decoder_1_out3, decoder_1_out2, decoder_1_out1, decoder_1_out0);
  or or_10 (or_10_out, or_5_out, decoder_1_out16, decoder_1_out17, decoder_1_out18, decoder_1_out19, decoder_1_out20, decoder_1_out21, decoder_1_out22, decoder_1_out23, decoder_1_out24, decoder_1_out25, decoder_1_out26, decoder_1_out27, decoder_1_out28, decoder_1_out29, decoder_1_out30, or_4_out, decoder_1_out31);
  or or_11 (or_11_out, decoder_1_out15, decoder_1_out14);
  or or_12 (or_12_out, decoder_1_out13, decoder_1_out12, decoder_1_out11, decoder_1_out10, decoder_1_out9, decoder_1_out8);
endmodule
